// Logisim project digital-voting.circ as structural Verilog: 1 circuit, main circuit main
module main (
  input  in_1
);

  wire A_out, B_out, C_out, deA_pin9, deA_pin10, deA_pin11, deA_pin12, deA_pin13, deA_pin14, deA_pin15,
       deB_pin9, deB_pin10, deB_pin11, deB_pin12, deB_pin13, deB_pin14, deB_pin15, deC_pin9, deC_pin10,
       deC_pin11, deC_pin12, deC_pin13, deC_pin14, deC_pin15, not_1_out, not_2_out, not_3_out, not_4_out,
       not_5_out, not_6_out, not_7_out, not_8_out, not_9_out, not_10_out, not_11_out, not_12_out, not_13_out,
       not_14_out, not_15_out, not_16_out, not_17_out, not_18_out, not_19_out, not_20_out, not_21_out,
       resetA_out, resetB_out, resetC_out;
  wire [3:0] countA_q, countB_q, countC_q;

  Button A (.out(A_out));
  Button B (.out(B_out));
  Button C (.out(C_out));
  Counter #(.max('hf), .width(4)) countA (
    .Q(countA_q), .clk(A_out), .clr(resetA_out));  // open: load, D, count, carry, up
  Button resetA (.out(resetA_out));
  Counter #(.max('h9), .width(4)) countB (
    .Q(countB_q), .clk(B_out), .clr(resetB_out));  // open: load, D, count, carry, up
  Button resetB (.out(resetB_out));
  Counter #(.max('hf), .width(4)) countC (
    .Q(countC_q), .clk(C_out), .clr(resetC_out));  // open: load, D, count, carry, up
  Button resetC (.out(resetC_out));
  _7447 #(.ShowInternalStructure("true")) deA (
    .pin1(countA_q[1]), .pin2(countA_q[2]), .pin6(countA_q[3]), .pin7(countA_q[0]), .pin15(deA_pin15),
    .pin14(deA_pin14), .pin13(deA_pin13), .pin12(deA_pin12), .pin11(deA_pin11), .pin10(deA_pin10),
    .pin9(deA_pin9));  // open: pin3, pin4, pin5
  _7447 #(.ShowInternalStructure("true")) deB (
    .pin1(countB_q[1]), .pin2(countB_q[2]), .pin5(in_1), .pin6(countB_q[3]), .pin7(countB_q[0]),
    .pin15(deB_pin15), .pin14(deB_pin14), .pin13(deB_pin13), .pin12(deB_pin12), .pin11(deB_pin11),
    .pin10(deB_pin10), .pin9(deB_pin9));  // open: pin3, pin4
  _7447 #(.ShowInternalStructure("true")) deC (
    .pin1(countC_q[1]), .pin2(countC_q[2]), .pin6(countC_q[3]), .pin7(countC_q[0]), .pin15(deC_pin15),
    .pin14(deC_pin14), .pin13(deC_pin13), .pin12(deC_pin12), .pin11(deC_pin11), .pin10(deC_pin10),
    .pin9(deC_pin9));  // open: pin3, pin4, pin5
  not not_1 (not_1_out, deC_pin11);
  not not_2 (not_2_out, deC_pin10);
  not not_3 (not_3_out, deC_pin9);
  not not_4 (not_4_out, deA_pin15);
  not not_5 (not_5_out, deA_pin14);
  not not_6 (not_6_out, deA_pin13);
  not not_7 (not_7_out, deA_pin12);
  not not_8 (not_8_out, deA_pin11);
  _7_Segment_Display voteA (
    .g(not_5_out), .f(not_4_out), .a(not_6_out), .b(not_7_out), .e(not_10_out), .d(not_9_out), .c(not_8_out));  // open: dp
  not not_9 (not_9_out, deA_pin10);
  not not_10 (not_10_out, deA_pin9);
  not not_11 (not_11_out, deB_pin15);
  not not_12 (not_12_out, deB_pin14);
  not not_13 (not_13_out, deB_pin13);
  not not_14 (not_14_out, deB_pin12);
  not not_15 (not_15_out, deB_pin11);
  _7_Segment_Display voteB (
    .g(not_12_out), .f(not_11_out), .a(not_13_out), .b(not_14_out), .e(not_17_out), .d(not_16_out),
    .c(not_15_out));  // open: dp
  not not_16 (not_16_out, deB_pin10);
  not not_17 (not_17_out, deB_pin9);
  not not_18 (not_18_out, deC_pin15);
  not not_19 (not_19_out, deC_pin14);
  not not_20 (not_20_out, deC_pin13);
  not not_21 (not_21_out, deC_pin12);
  _7_Segment_Display voteC (
    .g(not_19_out), .f(not_18_out), .a(not_20_out), .b(not_21_out), .e(not_3_out), .d(not_2_out),
    .c(not_1_out));  // open: dp
endmodule
